# Fritzing sketch Роботизированная система распределения грузов_Принципиальная схема (saved by Fritzing 0.9.9b)

parts:
  Nano = Arduino Nano (Rev3.0)
  DC = RioRand LM2596
  PJ = Power Jack [package=power_jack_combo]
  Pi_4B = Raspberry Pi 4B
  Cam = Rasberry Pi NIOR Camera [chip_label=IC package="DIP (Dual Inline) [THT]"]  # not connected
  Mr1 = Stepper Motor - Bipolar
  Dr1 = Pololu A4988 [package=SO16]
  Dr2 = Pololu A4988 [package=SO16]
  Mr2 = Stepper Motor - Bipolar
  C1 = Tantalum Capacitor [capacitance=1μF voltage=35V package="100 mil [THT, tantalum]"]

nets:
  GND: Nano.GND, DC.Pin_4, Pi_4B.GND, Dr1.GND#14, Dr2.GND#14, C1.-
  N1: Nano.D5, Dr2.DIR
  N2: Nano.D6, Dr2.STEP
  N3: Nano.D9, Dr1.DIR
  N4: Nano.D10, Dr1.STEP
  VIN: Nano.VIN, DC.Pin_3, Pi_4B.5V, C1.+
  N5: Nano.5V, Dr1.VMOT, Dr2.VMOT
  VDD: DC.Pin_1, PJ.PWR, Dr1.VDD, Dr2.VDD
  N6: DC.Pin_2, PJ.GND, Dr1.GND#8, Dr2.GND#8
  N7: Mr1.A, Dr1.2B
  N8: Mr1.C, Dr1.2A
  N9: Mr1.B, Dr1.1A
  N10: Mr1.D, Dr1.1B
  N11: Dr2.1B, Mr2.D
  N12: Dr2.1A, Mr2.B
  N13: Dr2.2A, Mr2.C
  N14: Dr2.2B, Mr2.A

notes:
  Power Jack
  Питание БП 12В 3A
  LM2596S
  DC DC Понижающий преобразователь
  Понижает и стабилизирует напряжение 12В => 5В 3А
  Raspberry Pi 4B
  Реализует алгоритмы системы распознавания. Получает управляющие команды от мобильного приложения по Bluetooth.
  OV5647
  Камера для Raspberry Pi
  Подключается по шине CSI
  Arduino Nano
  Управляет системой распределения: двигателем конвейера, датчиком наличия кубиков в зоне распознавания и сервоприводом сортировочной системы. Для защиты от помех и обратного тока используется конденсатор 0.1 мкФ
  17HE15-1504S
  Шаговый двигатель
  Приводит ленту конвейера в движение
  17HE15-1504S
  Шаговый двигатель
  Отвечает за распределение кубиков
  TMC2208
  Драйвер для шагового двигателя
  Управляет шаговым двигателем системы распределения
  Arduino Nano
  Управляет системой распределения: двигателем конвейера, датчиком наличия кубиков в зоне распознавания и сервоприводом сортировочной системы

custom parts:
  Rasberry Pi NIOR Camera: Camera
